# Fritzing sketch VertiBOT_ElectronicDiagram (saved by Fritzing 0.7.10b)
perfboards: 1

parts:
  qik_2s9v1 = mystery part, 12 pins [chip_label=?]
  Motores = rounded female pin header, 4 pins [form="♀ (female rounded)"]
  Transmisor_X-Bee = rounded female pin header, 4 pins [form="♀ (female rounded)"]
  Batería = male pin header, 2 pins [form="♂ (male)"]
  Micro = Arduino Nano v3.0
  Logic_Converte = Logic Level Converter
  Pulsador_2 = Pushbutton [package="[THT]"]
  R1 = Resistor [tolerance=±5% resistance=220 package=THT]
  Regulador = mystery part, 3 pins [chip_label=MCP1700]
  C1 = Ceramic Capacitor [capacitance=100nF package="100 mil [THT, multilayer]"]
  C2 = Ceramic Capacitor [capacitance=100nF package="100 mil [THT, multilayer]"]
  Ki = Trimmer Potentiometer [maximum_resistance=10kΩ package=THT]
  Kd = Trimmer Potentiometer [maximum_resistance=10kΩ package=THT]
  Kp = Trimmer Potentiometer [maximum_resistance=10kΩ package=THT]
  Pulsador_1 = Pushbutton [package="[THT]"]
  R6 = Resistor [tolerance=±5% resistance=220 package=THT]
  IMU = IMU Digital Combo Board 6DOF

nets (from the schematic view):
  N1: qik_2s9v1.pin1, Batería.pin1, Micro.VIN
  GND: qik_2s9v1.pin2, qik_2s9v1.pin12, Transmisor_X-Bee.pin1, Batería.pin2, Micro.GND, Logic_Converte.GND, Pulsador_2.Pin_3, Pulsador_2.Pin_4, Regulador.pin1, C1.0, Pulsador_1.Pin_3, IMU.GND
  N2: qik_2s9v1.pin3, Motores.pin4
  N3: qik_2s9v1.pin4, Motores.pin3
  N4: qik_2s9v1.pin5, Motores.pin2
  N5: qik_2s9v1.pin6, Motores.pin1
  N6: qik_2s9v1.pin8, Micro.D4
  N7: qik_2s9v1.pin9, Micro.D2
  N8: qik_2s9v1.pin10, Micro.D3
  5v: qik_2s9v1.pin11, Transmisor_X-Bee.pin2, Micro.+5V, Logic_Converte.HV, R1.Pin_0, Regulador.pin2, C2.1, Ki.leg2, Kd.leg2, Kp.leg2, R6.Pin_0
  N9: Transmisor_X-Bee.pin3, Micro.D0RX
  N10: Transmisor_X-Bee.pin4, Micro.D1TX
  D7: Micro.D7, Pulsador_1.Pin_1, Pulsador_1.Pin_2, R6.Pin_1
  D8: Micro.D8, Pulsador_2.Pin_1, Pulsador_2.Pin_2, R1.Pin_1
  A0: Micro.A0, Kp.wiper
  A1: Micro.A1, Ki.wiper
  A2: Micro.A2, Kd.wiper
  A4: Micro.A4, Logic_Converte.TX_HV
  A5: Micro.A5, Logic_Converte.TX2_HV
  3.3v: Logic_Converte.LV, Regulador.pin3, C1.1
  N11: Kd.leg1, Kp.leg1

notes:
  Conectores hembra
  Conectores macho
  MAF
  -
  +
  GND
  +5v
  Dout (Rx)
  Din (Tx)
  Potenciometros
  VertiBOT, Electronic Schematic , 1.0
